// Logisim project hw3.circ as structural Verilog: 2 circuits, main circuit CPU
module CPU (
);

  wire clock_1_out, nextpc_1_pcsrc, registerfile_1_p3, registerfile_1_p7, undriven, undriven_2, undriven_3,
       undriven_4, undriven_5;
  wire [4:0] mipsprogramrom_1_p2_2, mipsprogramrom_1_p2_3, mipsprogramrom_1_p2_4, mipsprogramrom_1_p2_5,
       multiplexer_2_out;
  wire [5:0] mipsprogramrom_1_p2, mipsprogramrom_1_p2_6;
  wire [19:0] mips_alu_1_p4;
  wire [29:0] incrementer_1_p2, multiplexer_1_out, nextpc_1_address, PC_q;
  wire [31:0] bit_extender_1_out, mips_ram_1_p4, multiplexer_3_out, registerfile_1_p1, registerfile_1_p8;
  wire [31:20] mips_alu_1_p4_2;

  Multiplexer #(.width(30), .enable("false")) multiplexer_1 (
    .in0(PC_q), .in1(nextpc_1_address), .out(multiplexer_1_out), .sel(nextpc_1_pcsrc));
  Clock clock_1 (.out(clock_1_out));
  Register #(.width(30), .trigger("falling")) PC (
    .D(multiplexer_1_out), .en(1'b1), .clk(clock_1_out), .Q(PC_q));  // open: clr
  // Incrementer #(.width(30)) incrementer_1: pin names not known; wires that end beside it: PC_q, incrementer_1_p2
  // MIPSProgramROM mipsprogramrom_1: pin names not known; wires that end beside it: {PC_q, 2'b00}, {mipsprogramrom_1_p2_6, mipsprogramrom_1_p2_5, mipsprogramrom_1_p2_4, mipsprogramrom_1_p2_3, mipsprogramrom_1_p2_2, mipsprogramrom_1_p2}
  Multiplexer #(.width(5), .enable("false")) multiplexer_2 (
    .in0(mipsprogramrom_1_p2_3), .in1(mipsprogramrom_1_p2_4), .out(multiplexer_2_out), .sel(undriven));
  // RegisterFile #(.trigger("falling")) registerfile_1: pin names not known; wires that end beside it: registerfile_1_p1, clock_1_out, registerfile_1_p3, multiplexer_2_out, mipsprogramrom_1_p2_2, mipsprogramrom_1_p2_3, registerfile_1_p7, registerfile_1_p8
  assign bit_extender_1_out = {{16{mipsprogramrom_1_p2_3[4]}}, {mipsprogramrom_1_p2_3, mipsprogramrom_1_p2_2, mipsprogramrom_1_p2}};  // Bit_Extender bit_extender_1
  Multiplexer #(.width(32), .enable("false")) multiplexer_3 (
    .in0(registerfile_1_p8), .in1(bit_extender_1_out), .out(multiplexer_3_out), .sel(undriven_2));
  // Mips_ALU mips_alu_1: pin names not known; wires that end beside it: registerfile_1_p7, multiplexer_3_out, mipsprogramrom_1_p2_5, {mips_alu_1_p4_2, mips_alu_1_p4}
  nextpc nextpc_1 (
    .PCSRC(nextpc_1_pcsrc),
    .IMM26({mipsprogramrom_1_p2_5, mipsprogramrom_1_p2_4, mipsprogramrom_1_p2_3, mipsprogramrom_1_p2_2, mipsprogramrom_1_p2}),
    .ZERO({mips_alu_1_p4_2, mips_alu_1_p4}), .J(undriven_5), .BNE(undriven_4), .BEQ(undriven_3),
    .INC_PC(incrementer_1_p2), .ADDRESS(nextpc_1_address));
  // MIPS_RAM mips_ram_1: pin names not known; wires that end beside it: mips_alu_1_p4, registerfile_1_p8, clock_1_out, mips_ram_1_p4, {mips_alu_1_p4_2, mips_alu_1_p4}
  Multiplexer #(.width(32), .enable("false")) multiplexer_4 (
    .in0({mips_alu_1_p4_2, mips_alu_1_p4}), .in1(mips_ram_1_p4), .out(registerfile_1_p1));  // open: sel
endmodule

module nextpc (
  input  [29:0] INC_PC,
  input  BEQ,
  input  BNE,
  input  J,
  input  [25:0] IMM26,
  input  [31:0] ZERO,
  output PCSRC,
  output [29:0] ADDRESS
);

  wire and_1_out, and_2_out, comparator_1_eq;
  wire [29:0] adder_1_out, bit_extender_1_out;

  assign bit_extender_1_out = {{14{IMM26[15]}}, IMM26[15:0]};  // Bit_Extender bit_extender_1
  Adder #(.width(30)) adder_1 (.a(INC_PC), .b(bit_extender_1_out), .out(adder_1_out));  // open: cin, cout
  Multiplexer #(.width(30), .enable("false")) multiplexer_1 (
    .in0(adder_1_out), .in1({INC_PC[29:26], IMM26}), .out(ADDRESS), .sel(J));
  and and_1 (and_1_out, ~comparator_1_eq, BNE);  // AND_Gate
  Comparator #(.width(32)) comparator_1 (.a({32{1'b0}}), .b(ZERO), .eq(comparator_1_eq));  // open: gt, lt
  or or_1 (PCSRC, and_1_out, J, and_2_out);
  and and_2 (and_2_out, comparator_1_eq, BEQ);
endmodule
